// Logisim project Ex1b.circ as structural Verilog: 1 circuit, main circuit main
module main (
  input  x,
  input  y,
  output s
);

  wire not_1_out, not_2_out;

  not not_1 (not_1_out, x);
  not not_2 (not_2_out, y);
  nand nand_1 (s, not_1_out, not_2_out);
endmodule
