// Logisim project Ex3a.circ as structural Verilog: 1 circuit, main circuit main
module main (
  input  a,
  input  b,
  input  c,
  output T
);

  wire nand_1_out, nand_2_out, nand_3_out;

  nand nand_1 (nand_1_out, a, b);
  nand nand_2 (nand_2_out, a, c);
  nand nand_3 (nand_3_out, b, c);
  nand nand_4 (T, nand_1_out, nand_2_out, nand_3_out);
endmodule
